# Fritzing sketch Sketch (saved by Fritzing 0.9.5d)
breadboards: 1

parts:
  U1 = NodeMCU V3.0
  QNC5883L = Triple Axis Magnetometer - HMC5883 Breakout

nets:
  N1: U1.D1, QNC5883L.SCL
  N2: U1.D2, QNC5883L.SDA
  N3: U1.GND#6, U1.GND#13, U1.GND#16, U1.GND#33, QNC5883L.GND
  VIN: U1.Vin, QNC5883L.VCC

custom parts:
  NodeMCU V3.0: ESP8266 based NodeMCU
